# Fritzing sketch LEDColorSchematic (saved by Fritzing 0.8.5b)
circuit board: 8.46667cm x 5.64444cm
breadboards: 1

parts:
  IC1 = L293D [package=THT]
  J1 = Power Jack [package=power_jack_pth_lock]
  Part1 = Arduino Nano (Rev3.0)

nets:
  GND: IC1.Enable_1, IC1.0V, IC1.+Vmotor, IC1.Enable_2, J1.GND, J1.GNDBREAK, J1.PWR, Part1.GND
  N1: IC1.In_1, Part1.A1
  N2: IC1.In_2, Part1.A0
  N3: IC1.In_4, Part1.A2
  N4: IC1.+V, Part1.VIN
